// Logisim project Ctl_SP_Address.circ as structural Verilog: 1 circuit, main circuit SP_Address
module SP_Address (
  input  [31:0] Stack_Pointer,
  input  [15:0] Instruction,
  input  Enable,
  output Write_Enable,
  output [31:0] New_Stack_Pointer
);

  wire bitselector_1_out;
  wire [6:0] bit_extender_1_out;
  wire [31:0] bit_extender_2_out, imm7, multiplexer_1_out, pop, push;

  Bit_Extender #(.in_width(16), .out_width(7), .\type ("zero")) bit_extender_1 (
    .in(Instruction), .out(bit_extender_1_out));
  Multiplexer #(.width(32)) multiplexer_1 (.in0(push), .in1(pop), .out(multiplexer_1_out), .sel(bitselector_1_out));
  BitSelector #(.width(16)) bitselector_1 (.in(Instruction), .out(bitselector_1_out), .sel(4'b0111));
  assign bit_extender_2_out = {{25{1'b0}}, bit_extender_1_out};  // Bit_Extender bit_extender_2
  Adder #(.width(32)) adder_1 (.a(Stack_Pointer), .b(imm7), .out(push));  // open: cin, cout
  Subtractor #(.width(32)) subtractor_1 (.a(Stack_Pointer), .b(imm7), .out(pop));  // open: bin, bout
  Multiplexer #(.width(32)) multiplexer_2 (
    .in0({32{1'b0}}), .in1(multiplexer_1_out), .out(New_Stack_Pointer), .sel(Enable));
  Shifter #(.width(32)) shifter_1 (.in(bit_extender_2_out), .\dist (5'b00010), .out(imm7));

  assign Write_Enable = Enable;

  // Notes on the sheet:
  //   Pull output low on Enable = 0
endmodule
