// Logisim project ALU.circ as structural Verilog: 1 circuit, main circuit ALU
module ALU (
  input  [31:0] A,
  input  [31:0] B,
  input  [4:0] Shift,
  input  CarryIn,
  input  [3:0] Codop,
  output [31:0] S,
  output [3:0] Flags
);

  wire and_4_out, and_5_out, and_6_out, and_7_out, and_8_out, and_9_out, and_10_out, and_11_out, and_16_out,
       and_17_out, and_18_out, and_19_out, and_20_out, Borrow_cmp, borrow_sbc_raw, C_adc_raw, c_add,
       C_cmn_raw, C_cmp, C_lsl, C_lsr_asr, C_ror_sel, C_sbc, C_shift, C_sub, isADC, isASR, isCMN, isCMP,
       isLSL, isLSR, isNoWrite, isROR, isRSB, isSBC, isTST, not_1_out, not_6_out, or_2_out, or_6_out,
       or_7_out, or_9_out, or_11_out, or_12_out, or_13_out, V_add, V_rsb, V_sub, xor_2_out, xor_3_out,
       xor_4_out, xor_5_out;
  wire [4:0] ShiftMinus1;
  wire [30:0] R, tmpLSL;
  wire [31:0] adder_1_out, adder_2_out, and_1_out, and_2_out, and_3_out, multiplier_1_out, negator_1_out,
       not_2_out, not_3_out, or_1_out, shifter_1_out, shifter_2_out, shifter_3_out, shifter_4_out,
       subtractor_1_out, subtractor_2_out, xor_1_out;
  wire [31:1] tmpRight;

  not not_1 (not_1_out, CarryIn);
  assign and_1_out = A & B;  // AND_Gate and_1, 32 bits wide
  assign xor_1_out = A ^ B;  // XOR_Gate xor_1, 32 bits wide
  Shifter #(.width(32)) shifter_1 (.in(B), .\dist (Shift), .out(shifter_1_out));
  Shifter #(.shift("lr"), .width(32)) shifter_2 (.in(B), .\dist (Shift), .out(shifter_2_out));
  Shifter #(.shift("ar"), .width(32)) shifter_3 (.in(B), .\dist (Shift), .out(shifter_3_out));
  Adder #(.width(32)) adder_1 (.a(A), .b(B), .out(adder_1_out), .cin(CarryIn), .cout(C_adc_raw));
  // Probe on C_adc_raw
  Subtractor #(.width(32)) subtractor_1 (.a(B), .b(A), .out(subtractor_1_out), .bin(not_1_out), .bout(borrow_sbc_raw));
  Shifter #(.shift("rr"), .width(32)) shifter_4 (.in(B), .\dist (Shift), .out(shifter_4_out));
  assign and_2_out = A & B;  // AND_Gate and_2, 32 bits wide
  Negator #(.width(32)) negator_1 (.in(A), .out(negator_1_out));
  Subtractor #(.width(32)) subtractor_2 (.a(B), .b(A), .out(subtractor_2_out), .bout(Borrow_cmp));  // open: bin
  Adder #(.width(32)) adder_2 (.a(A), .b(B), .out(adder_2_out), .cout(C_cmn_raw));  // open: cin
  // Probe on C_cmn_raw
  assign or_1_out = A | B;  // OR_Gate or_1, 32 bits wide
  Multiplier #(.width(32)) multiplier_1 (.a(A), .b(B), .out(multiplier_1_out));  // open: cin, cout
  assign not_2_out = ~A;  // NOT_Gate not_2, 32 bits wide
  assign not_3_out = ~A;  // NOT_Gate not_3, 32 bits wide
  assign and_3_out = not_2_out & B;  // AND_Gate and_3, 32 bits wide
  Multiplexer #(.select(4), .width(32)) multiplexer_1 (
    .in0(and_1_out), .in1(xor_1_out), .in2(shifter_1_out), .in3(shifter_2_out), .in4(shifter_3_out),
    .in5(adder_1_out), .in6(subtractor_1_out), .in7(shifter_4_out), .in8(and_2_out), .in9(negator_1_out),
    .in10(subtractor_2_out), .in11(adder_2_out), .in12(or_1_out), .in13(multiplier_1_out), .in14(and_3_out),
    .in15(not_3_out), .out({Flags[3], R}), .sel(Codop));
  // Probe on {Flags[3], R}
  Comparator #(.width(4)) comparator_1 (.a(Codop), .b(4'b1000), .eq(isTST));  // open: gt, lt
  Comparator #(.width(4)) comparator_2 (.a(Codop), .b(4'b0010), .eq(isLSL));  // open: gt, lt
  Comparator #(.width(4)) comparator_3 (.a(Codop), .b(4'b0011), .eq(isLSR));  // open: gt, lt
  Comparator #(.width(4)) comparator_4 (.a(Codop), .b(4'b0100), .eq(isASR));  // open: gt, lt
  Comparator #(.width(4)) comparator_5 (.a(Codop), .b(4'b0101), .eq(isADC));  // open: gt, lt
  Comparator #(.width(4)) comparator_6 (.a(Codop), .b(4'b0110), .eq(isSBC));  // open: gt, lt
  Comparator #(.width(4)) comparator_7 (.a(Codop), .b(4'b0111), .eq(isROR));  // open: gt, lt
  Comparator #(.width(4)) comparator_8 (.a(Codop), .b(4'b1001), .eq(isRSB));  // open: gt, lt
  Comparator #(.width(4)) comparator_9 (.a(Codop), .b(4'b1010), .eq(isCMP));  // open: gt, lt
  Comparator #(.width(4)) comparator_10 (.a(Codop), .b(4'b1011), .eq(isCMN));  // open: gt, lt
  Comparator #(.width(32)) comparator_11 (.a({Flags[3], R}), .b({32{1'b0}}), .eq(Flags[2]));  // open: gt, lt
  Multiplexer #(.width(32)) multiplexer_2 (.in0({Flags[3], R}), .in1(B), .out(S), .sel(isNoWrite));
  and and_4 (and_4_out, isADC, C_adc_raw);
  and and_5 (and_5_out, isCMN, C_cmn_raw);
  or or_2 (or_2_out, isTST, isCMP);
  not not_4 (C_cmp, Borrow_cmp);
  not not_5 (C_sbc, borrow_sbc_raw);
  and and_6 (and_6_out, isCMP, C_cmp);
  and and_7 (and_7_out, isSBC, C_sbc);
  Subtractor #(.width(5)) subtractor_3 (.a(Shift), .b(5'b00001), .out(ShiftMinus1));  // open: bin, bout
  Shifter #(.width(32)) shifter_5 (.in(B), .\dist (ShiftMinus1), .out({C_lsl, tmpLSL}));
  Shifter #(.shift("lr"), .width(32)) shifter_6 (.in(B), .\dist (ShiftMinus1), .out({tmpRight, C_lsr_asr}));
  Comparator #(.width(4)) comparator_12 (.a(Codop), .b(4'b0111), .eq(isROR));  // open: gt, lt
  and and_8 (and_8_out, isLSL, C_lsl);
  and and_9 (and_9_out, isLSR, C_lsr_asr);
  and and_10 (and_10_out, isASR, C_lsr_asr);
  and and_11 (and_11_out, isROR, Flags[3]);
  or or_3 (isNoWrite, or_2_out, isCMN);
  or or_4 (c_add, and_4_out, and_5_out);
  or or_5 (C_sub, and_6_out, and_7_out);
  or or_6 (or_6_out, c_add, C_sub);
  or or_7 (or_7_out, and_8_out, and_9_out);
  and and_12 (C_ror_sel, isROR, Flags[3]);
  or or_8 (Flags[1], or_6_out, C_shift);
  or or_9 (or_9_out, or_7_out, and_10_out);
  xor xor_2 (xor_2_out, A[31], B[31]);
  xor xor_3 (xor_3_out, A[31], Flags[3]);
  xor xor_4 (xor_4_out, A[31], B[31]);
  xor xor_5 (xor_5_out, B[31], Flags[3]);
  and and_13 (V_rsb, A[31], Flags[3]);
  or or_10 (C_shift, or_9_out, and_11_out);
  not not_6 (not_6_out, xor_2_out);
  and and_14 (V_sub, xor_4_out, xor_5_out);
  and and_15 (V_add, not_6_out, xor_3_out);
  and and_16 (and_16_out, isADC, V_add);
  and and_17 (and_17_out, isCMN, V_add);
  and and_18 (and_18_out, isCMP, V_sub);
  and and_19 (and_19_out, isSBC, V_sub);
  and and_20 (and_20_out, isRSB, V_rsb);
  or or_11 (or_11_out, and_16_out, and_17_out);
  or or_12 (or_12_out, and_18_out, and_19_out);
  or or_13 (or_13_out, or_11_out, or_12_out);
  or or_14 (Flags[0], or_13_out, and_20_out);

  // Other names for the same wires on the sheet: V = Flags[0]; C = Flags[1]; Z = Flags[2]; N = Flags[3];
  //   R[31] = Flags[3]; tmpLSL[31] = C_lsl; tmpRight[0] = C_lsr_asr

  // Notes on the sheet:
  //   Note: for ROR, C = N
  //   Note 2: assume that shift > 0 for LSL and LSR
endmodule
