// Logisim project Ctl_Conditional.circ as structural Verilog: 1 circuit, main circuit Conditional
module Conditional (
  input  Enable,
  input  [15:0] Instruction,
  input  Z,
  input  C,
  input  N,
  input  V,
  output [10:0] Offset,
  output Verified
);

  wire AL, BIT13, CC, GE, GT, HI, isBcond, LE, LS, LT, multiplexer_1_out, multiplexer_2_out,
       multiplexer_3_out, NE, not_6_out, PL, VC;

  not not_1 (NE, Z);
  not not_2 (CC, C);
  not not_3 (PL, N);
  not not_4 (VC, V);
  and and_1 (HI, C, NE);
  or or_1 (LS, CC, Z);
  not not_5 (LT, GE);
  and and_2 (GT, NE, GE);
  or or_2 (LE, Z, LT);
  Comparator #(.width(1)) comparator_1 (.a(N), .b(V), .eq(GE));  // open: gt, lt
  Multiplexer #(.select(4)) multiplexer_1 (
    .in0(Z), .in1(NE), .in2(C), .in3(CC), .in4(N), .in5(PL), .in6(V), .in7(VC), .in8(HI), .in9(LS),
    .in10(GE), .in11(LT), .in12(GT), .in13(LE), .in14(AL), .out(multiplexer_1_out), .sel(Instruction[11:8]));  // open: in15
  Multiplexer multiplexer_2 (.in0(multiplexer_1_out), .in1(1'b1), .out(multiplexer_2_out), .sel(not_6_out));
  not not_6 (not_6_out, Instruction[12]);
  Multiplexer multiplexer_3 (.in0(1'b0), .in1(multiplexer_2_out), .out(multiplexer_3_out), .sel(Enable));
  assign Offset = {{3{Instruction[7]}}, Instruction[7:0]};  // Bit_Extender bit_extender_1
  not not_7 (BIT13, Instruction[13]);
  and and_3 (Verified, multiplexer_3_out, isBcond);
  and and_4 (isBcond, Instruction[12], BIT13, Instruction[14], Instruction[15]);

  // Other names for the same wires on the sheet: CS = C; EQ = Z; imm8[7:0] = Instruction[7:0];
  //   imm11[10:0] = Instruction[10:0]; COND[3:0] = Instruction[11:8]; BIT12 = Instruction[12];
  //   BIT14 = Instruction[14]; BIT15 = Instruction[15]; MI = N; VS = V
endmodule
