// Logisim project Ctl_Flags_APSR.circ as structural Verilog: 1 circuit, main circuit Flags_APSR
module Flags_APSR (
  input  [3:0] Update_Mask,
  input  [3:0] Flags_In,
  input  Clk,
  input  Rst,
  output [3:0] Flags_Out
);

  wire [3:0] NextFlag;

  // Probe on Flags_In
  // Probe on Update_Mask
  Register #(.width(4)) register_1 (.D(NextFlag), .en(1'b1), .clk(Clk), .Q(Flags_Out), .clr(Rst));
  Multiplexer multiplexer_1 (.in0(Flags_Out[0]), .in1(Flags_In[0]), .out(NextFlag[0]), .sel(Update_Mask[0]));
  Multiplexer multiplexer_2 (.in0(Flags_Out[1]), .in1(Flags_In[1]), .out(NextFlag[1]), .sel(Update_Mask[1]));
  Multiplexer multiplexer_3 (.in0(Flags_Out[2]), .in1(Flags_In[2]), .out(NextFlag[2]), .sel(Update_Mask[2]));
  Multiplexer multiplexer_4 (.in0(Flags_Out[3]), .in1(Flags_In[3]), .out(NextFlag[3]), .sel(Update_Mask[3]));
endmodule
