// Logisim project Ctl_Load_Store.circ as structural Verilog: 1 circuit, main circuit Load_Store
module Load_Store (
  input  [15:0] Instruction,
  input  Clk,
  input  Reset,
  input  [31:0] Stack_Pointer,
  input  Enable,
  output PC_Hold,
  output [2:0] Rmd,
  output Load,
  output [31:0] RAM_Addr_calc,
  output Store
);

  wire and_1_out, and_2_out, and_5_out, Ldr, Load_internal, Load_row, not_1_out, not_2_out, not_3_out,
       opcode, PC_Hold_internal;
  wire [2:0] Rmd_internal;
  wire [7:0] offset;
  wire [14:12] register_1_q;
  wire [31:0] adder_1_out, bit_extender_1_out, shifter_1_out;

  not not_1 (not_1_out, PC_Hold_internal);
  assign bit_extender_1_out = {{24{1'b0}}, offset};  // Bit_Extender bit_extender_1
  Shifter #(.width(32)) shifter_1 (.in(bit_extender_1_out), .\dist (5'b00010), .out(shifter_1_out));
  Register #(.width(16)) register_1 (
    .D(Instruction), .en(not_1_out), .clk(Clk), .Q({opcode, register_1_q, Ldr, Rmd_internal, offset}),
    .clr(Reset));
  Adder #(.width(32)) adder_1 (.a(Stack_Pointer), .b(shifter_1_out), .out(adder_1_out));  // open: cin, cout
  D_Flip_Flop d_ff_1 (.D(Load_row), .clk(Clk), .Q(Load_internal), .reset(Reset));  // open: Qn, preset
  not not_2 (not_2_out, Load_internal);
  and and_1 (and_1_out, opcode, Enable);
  Multiplexer #(.width(32)) multiplexer_1 (.in0({32{1'b0}}), .in1(adder_1_out), .out(RAM_Addr_calc), .sel(Enable));
  and and_2 (and_2_out, and_1_out, Ldr);
  and and_3 (Load_row, not_2_out, and_2_out);
  or or_1 (PC_Hold_internal, Load_internal, Load_row);
  Multiplexer #(.width(3)) multiplexer_2 (.in0(3'b000), .in1(Rmd_internal), .out(Rmd), .sel(Enable));
  and and_4 (Load, Load_internal, Enable);
  and and_5 (and_5_out, Enable, opcode);
  not not_3 (not_3_out, Ldr);
  and and_6 (Store, and_5_out, not_3_out);
  and and_7 (PC_Hold, PC_Hold_internal, Enable);
endmodule
