// Logisim project Ctl_Opcode_Decoder.circ as structural Verilog: 1 circuit, main circuit Opcode_Decoder
module Opcode_Decoder (
  input  [5:0] Opcode,
  output Shift,
  output Data_Processing,
  output Load_Store,
  output SP_Address,
  output Conditional
);

  Comparator #(.width(3)) comparator_1 (.a(Opcode[5:3]), .b(3'b000), .eq(Shift));  // open: gt, lt
  Comparator #(.width(6)) comparator_2 (.a(Opcode), .b(6'b010000), .eq(Data_Processing));  // open: gt, lt
  Comparator #(.width(3)) comparator_3 (.a(Opcode[5:3]), .b(3'b100), .eq(Load_Store));  // open: gt, lt
  Comparator #(.width(6)) comparator_4 (.a(Opcode), .b(6'b101100), .eq(SP_Address));  // open: gt, lt
  Comparator #(.width(4)) comparator_5 (.a(Opcode[5:2]), .b(4'b1100), .eq(Conditional));  // open: gt, lt

  // Notes on the sheet:
  //   Shift, add, sub, mov
  //   Load/Store
  //   SP Address
  //   Conditional branch
  //   Data Processing
endmodule
