// Logisim project Ctl_Shift_Add_Sub_Mov.circ as structural Verilog: 1 circuit, main circuit Shift_Add_Sub_Mov
module Shift_Add_Sub_Mov (
  input  Enable,
  input  [15:0] Instruction,
  output [31:0] Imm32,
  output Carry,
  output [2:0] Rm,
  output [2:0] Rn,
  output [2:0] Rd,
  output [3:0] Flags_Update_Mask,
  output [4:0] Imm5,
  output [3:0] ALU_Opcode,
  output Imm32_Enable
);

  wire ADD_IMM3, ADD_IMM8, ADD_REG, ASR, CMP, LSL, LSR, MOV, or_2_out, or_3_out, or_4_out, or_5_out,
       or_6_out, SUB_IMM3, SUB_IMM8, SUB_REG;
  wire [2:0] bit_extender_15_out, bit_extender_16_out, bit_extender_17_out;
  wire [3:0] and_1_out, and_2_out, and_3_out, and_4_out, and_5_out, and_6_out, and_7_out, and_20_out,
       and_21_out, and_22_out, and_23_out, bit_extender_1_out, bit_extender_2_out, bit_extender_3_out,
       bit_extender_4_out, bit_extender_5_out, bit_extender_6_out, bit_extender_7_out, bit_extender_8_out,
       bit_extender_9_out, bit_extender_10_out, bit_extender_11_out, bit_extender_14_out,
       bit_extender_19_out, bit_extender_20_out, bit_extender_21_out, bit_extender_22_out,
       bit_extender_23_out, h, hr, or_1_out, or_7_out, z, zr;
  wire [4:0] bit_extender_18_out;
  wire [31:0] bit_extender_12_out, bit_extender_13_out;

  Comparator #(.width(5)) comparator_1 (.a(Instruction[15:11]), .b({5{1'b0}}), .eq(LSL));  // open: gt, lt
  Comparator #(.width(5)) comparator_2 (.a(Instruction[15:11]), .b(5'b00001), .eq(LSR));  // open: gt, lt
  Comparator #(.width(5)) comparator_3 (.a(Instruction[15:11]), .b(5'b00010), .eq(ASR));  // open: gt, lt
  Comparator #(.width(5)) comparator_4 (.a(Instruction[15:11]), .b(5'b00100), .eq(MOV));  // open: gt, lt
  Comparator #(.width(5)) comparator_5 (.a(Instruction[15:11]), .b(5'b00101), .eq(CMP));  // open: gt, lt
  Comparator #(.width(5)) comparator_6 (.a(Instruction[15:11]), .b(5'b00110), .eq(ADD_IMM8));  // open: gt, lt
  Comparator #(.width(5)) comparator_7 (.a(Instruction[15:11]), .b(5'b00111), .eq(SUB_IMM8));  // open: gt, lt
  assign bit_extender_1_out = {{3{LSL}}, LSL};  // Bit_Extender bit_extender_1
  assign bit_extender_2_out = {{3{LSR}}, LSR};  // Bit_Extender bit_extender_2
  assign bit_extender_3_out = {{3{ASR}}, ASR};  // Bit_Extender bit_extender_3
  assign bit_extender_4_out = {{3{MOV}}, MOV};  // Bit_Extender bit_extender_4
  assign bit_extender_5_out = {{3{CMP}}, CMP};  // Bit_Extender bit_extender_5
  assign bit_extender_6_out = {{3{ADD_IMM8}}, ADD_IMM8};  // Bit_Extender bit_extender_6
  assign bit_extender_7_out = {{3{SUB_IMM8}}, SUB_IMM8};  // Bit_Extender bit_extender_7
  Comparator #(.width(7)) comparator_8 (.a(Instruction[15:9]), .b(7'b0001110), .eq(ADD_IMM3));  // open: gt, lt
  Comparator #(.width(7)) comparator_9 (.a(Instruction[15:9]), .b(7'b0001111), .eq(SUB_IMM3));  // open: gt, lt
  Comparator #(.width(7)) comparator_10 (.a(Instruction[15:9]), .b(7'b0001100), .eq(ADD_REG));  // open: gt, lt
  Comparator #(.width(7)) comparator_11 (.a(Instruction[15:9]), .b(7'b0001101), .eq(SUB_REG));  // open: gt, lt
  assign and_1_out = bit_extender_1_out & 4'b0010;  // AND_Gate and_1, 4 bits wide
  assign and_2_out = bit_extender_2_out & 4'b0011;  // AND_Gate and_2, 4 bits wide
  assign and_3_out = bit_extender_3_out & 4'b0100;  // AND_Gate and_3, 4 bits wide
  assign and_4_out = bit_extender_4_out & 4'b0110;  // AND_Gate and_4, 4 bits wide
  assign and_5_out = bit_extender_5_out & 4'b0110;  // AND_Gate and_5, 4 bits wide
  assign and_6_out = bit_extender_6_out & 4'b0101;  // AND_Gate and_6, 4 bits wide
  assign and_7_out = bit_extender_7_out & 4'b0110;  // AND_Gate and_7, 4 bits wide
  assign bit_extender_8_out = {{3{ADD_IMM3}}, ADD_IMM3};  // Bit_Extender bit_extender_8
  assign bit_extender_9_out = {{3{SUB_IMM3}}, SUB_IMM3};  // Bit_Extender bit_extender_9
  assign bit_extender_10_out = {{3{ADD_REG}}, ADD_REG};  // Bit_Extender bit_extender_10
  assign bit_extender_11_out = {{3{SUB_REG}}, SUB_REG};  // Bit_Extender bit_extender_11
  assign bit_extender_12_out = {{24{Instruction[7]}}, Instruction[7:0]};  // Bit_Extender bit_extender_12
  assign bit_extender_13_out = {{31{Imm32_Enable}}, Imm32_Enable};  // Bit_Extender bit_extender_13
  assign z = bit_extender_8_out & 4'b0101;  // AND_Gate and_8, 4 bits wide
  assign h = bit_extender_9_out & 4'b0110;  // AND_Gate and_9, 4 bits wide
  assign zr = bit_extender_10_out & 4'b0101;  // AND_Gate and_10, 4 bits wide
  assign hr = bit_extender_11_out & 4'b0110;  // AND_Gate and_11, 4 bits wide
  assign Imm32 = bit_extender_12_out & bit_extender_13_out;  // AND_Gate and_12, 32 bits wide
  assign bit_extender_14_out = {{3{Enable}}, Enable};  // Bit_Extender bit_extender_14
  assign or_1_out = zr | h | and_1_out | and_5_out | and_2_out | and_6_out | and_3_out | and_7_out | and_4_out | z | zr;  // OR_Gate or_1, 4 bits wide
  assign ALU_Opcode = or_1_out & bit_extender_14_out;  // AND_Gate and_13, 4 bits wide
  assign bit_extender_15_out = {{2{Enable}}, Enable};  // Bit_Extender bit_extender_15
  assign bit_extender_16_out = {{2{Enable}}, Enable};  // Bit_Extender bit_extender_16
  or or_2 (or_2_out, MOV, CMP, ADD_IMM8, SUB_IMM8, ADD_IMM3, SUB_IMM3);
  assign Rm = Instruction[8:6] & bit_extender_15_out;  // AND_Gate and_14, 3 bits wide
  assign Rn = Instruction[5:3] & bit_extender_16_out;  // AND_Gate and_15, 3 bits wide
  assign bit_extender_17_out = {{2{Enable}}, Enable};  // Bit_Extender bit_extender_17
  assign bit_extender_18_out = {{4{Enable}}, Enable};  // Bit_Extender bit_extender_18
  assign Rd = Instruction[2:0] & bit_extender_17_out;  // AND_Gate and_16, 3 bits wide
  assign Imm5 = Instruction[10:6] & bit_extender_18_out;  // AND_Gate and_17, 5 bits wide
  and and_18 (Imm32_Enable, Enable, or_2_out);
  or or_3 (or_3_out, LSL, LSR, ASR);
  or or_4 (or_4_out, ADD_IMM8, ADD_IMM3, ADD_REG);
  or or_5 (or_5_out, SUB_IMM8, SUB_IMM3, SUB_REG, CMP);
  or or_6 (or_6_out, SUB_IMM8, SUB_IMM3, SUB_REG, CMP);
  assign bit_extender_19_out = {{3{or_3_out}}, or_3_out};  // Bit_Extender bit_extender_19
  assign bit_extender_20_out = {{3{or_4_out}}, or_4_out};  // Bit_Extender bit_extender_20
  assign bit_extender_21_out = {{3{or_5_out}}, or_5_out};  // Bit_Extender bit_extender_21
  assign bit_extender_22_out = {{3{MOV}}, MOV};  // Bit_Extender bit_extender_22
  and and_19 (Carry, Enable, or_6_out);
  assign and_20_out = bit_extender_19_out & 4'b1110;  // AND_Gate and_20, 4 bits wide
  assign and_21_out = bit_extender_20_out & 4'b1111;  // AND_Gate and_21, 4 bits wide
  assign and_22_out = bit_extender_21_out & 4'b1111;  // AND_Gate and_22, 4 bits wide
  assign and_23_out = bit_extender_22_out & 4'b1010;  // AND_Gate and_23, 4 bits wide
  assign or_7_out = and_20_out | and_21_out | and_22_out | and_23_out;  // OR_Gate or_7, 4 bits wide
  assign bit_extender_23_out = {{3{Enable}}, Enable};  // Bit_Extender bit_extender_23
  assign Flags_Update_Mask = or_7_out & bit_extender_23_out;  // AND_Gate and_24, 4 bits wide

  // Other names for the same wires on the sheet: E = Enable; lien[6:0] = Instruction[15:9]

  // Notes on the sheet:
  //   Note 3: Imm32_Enable forces the use of the immediate for Rm register
  //   Note 2: MOV uses RSB ALU opcode with Imm8 reversed so that it is copied to output register
  //   Note: ALU uses Rn register for shifts. Use Rn instead of Rm for shifts (immediate) here too
  //   only ADD and SUB use Rm
  //   Enable carry for SUB since it is reversed in ALU
  //   ALU will use Imm32 instead of Rm
  //   Pull output low on Enable = 0
endmodule
